// Logisim project Dodge_39_em_all_1_0.circ as structural Verilog: 11 circuits, main circuit main
module main (
);

  wire button, button_2_out, button_out, c1, c2, c3, c4, cdm_8_mark5_1_p1, cdm_8_mark5_1_p3,
       cdm_8_mark5_1_p6, cdm_8_mark5_1_p8, cdm_8_mark5_1_p10, cdm_8_mark5_1_p12, cdm_8_mark5_1_p14,
       cdm_8_mark5_1_p15, cdm_8_mark5_1_p20, clock_1_out, clock_2_out, clock_3_out, code, data, death,
       graph_clock, hp_1_cell_1_1, hp_1_cell_1_2, hp_1_cell_2_1, hp_1_cell_2_2, hp_1_cell_3_1, hp_1_cell_3_2,
       hp_1_cell_4_1, hp_1_cell_4_2, IOsel, keyboard_translator_1_left, keyboard_translator_1_right,
       keyboard_translator_1_start_stop, ld, line_controler_1_need_value, line_controler_2_need_value,
       line_controler_3_need_value, line_controler_4_need_value, not_1_out, not_2_out, or_1_out, or_2_out,
       or_3_out, or_5_out, proc_clock, ran_clock, sel, St_ch, start_stop_out, state_control_1_state;
  wire [1:0] r;
  wire [2:0] fig;
  wire [3:0] light_years_count_1_hundred, light_years_count_1_ten, light_years_count_1_thousand,
       light_years_count_1_unit, query_filter_1_filtered;
  wire [6:0] keyboard_1_data;
  wire [7:0] A, cdm_8_mark5_1_p18, cdm_8_mark5_1_p19, controlled_buffer_4_out, D, io_device_1_out;
  wire [7:3] IOdata;
  wire [11:0] player_control_1_line_1, player_control_1_line_2, player_control_1_line_3,
       player_control_1_line_4;
  wire [31:0] line_controler_1_line_1, line_controler_1_line_2, line_controler_1_line_3,
       line_controler_2_line_1, line_controler_2_line_2, line_controler_2_line_3, line_controler_3_line_1,
       line_controler_3_line_2, line_controler_3_line_3, line_controler_4_line_1, line_controler_4_line_2,
       line_controler_4_line_3;

  or or_1 (or_1_out, death, button);
  Clock clock_1 (.out(clock_1_out));
  Clock #(.lowDuration(31)) clock_2 (.out(clock_2_out));
  Clock #(.lowDuration(45)) clock_3 (.out(clock_3_out));
  state_control state_control_1 (.change_state(or_1_out), .state(state_control_1_state), .state_changed(St_ch));
  assign proc_clock = state_control_1_state ? clock_1_out : 1'bz;  // Controlled_Buffer controlled_buffer_1
  Pull_Resistor pull_resistor_1 (.node(proc_clock));
  assign ran_clock = state_control_1_state ? clock_2_out : 1'bz;  // Controlled_Buffer controlled_buffer_2
  Pull_Resistor pull_resistor_2 (.node(ran_clock));
  Pull_Resistor pull_resistor_3 (.node(graph_clock));
  assign graph_clock = state_control_1_state ? clock_3_out : 1'bz;  // Controlled_Buffer controlled_buffer_3
  Keyboard keyboard_1 (.clk(clock_1_out), .data(keyboard_1_data));  // open: re, clr, avail
  or or_2 (or_2_out, button_out, keyboard_translator_1_left);
  keyboard_translator keyboard_translator_1 (
    .keyboard(keyboard_1_data), .left(keyboard_translator_1_left), .right(keyboard_translator_1_right),
    .start_stop(keyboard_translator_1_start_stop));
  or or_3 (or_3_out, keyboard_translator_1_right, button_2_out);
  player_control player_control_1 (
    .restart(St_ch), .active_line_code(r), .left_button(or_2_out), .right_button(or_3_out),
    .line_1(player_control_1_line_1), .line_2(player_control_1_line_2), .line_3(player_control_1_line_3),
    .line_4(player_control_1_line_4));
  Hex_Digit_Display hex_digit_display_1 (.value(light_years_count_1_thousand));  // open: dp
  light_years_count light_years_count_1 (
    .thousand(light_years_count_1_thousand), .hundred(light_years_count_1_hundred),
    .ten(light_years_count_1_ten), .unit(light_years_count_1_unit), .clock(graph_clock), .restart(St_ch));
  or or_4 (button, start_stop_out, keyboard_translator_1_start_stop);
  Hex_Digit_Display hex_digit_display_2 (.value(light_years_count_1_ten));  // open: dp
  Hex_Digit_Display hex_digit_display_3 (.value(light_years_count_1_hundred));  // open: dp
  Button u_button (.out(button_out));
  Hex_Digit_Display hex_digit_display_4 (.value(light_years_count_1_unit));  // open: dp
  Button start_stop (.out(start_stop_out));
  Button button_2 (.out(button_2_out));
  DotMatrix #(.matrixcols(12), .matrixrows(32)) dotmatrix_1 (
    .col0(line_controler_1_line_1), .col1(line_controler_1_line_2), .col2(line_controler_1_line_3),
    .col3(line_controler_2_line_1), .col4(line_controler_2_line_2), .col5(line_controler_2_line_3),
    .col6(line_controler_3_line_1), .col7(line_controler_3_line_2), .col8(line_controler_3_line_3),
    .col9(line_controler_4_line_1), .col10(line_controler_4_line_2), .col11(line_controler_4_line_3));
  line_controler line_controler_1 (
    .figure(fig), .Querry_Addr(IOdata[6:4]), .Line_Addr(3'b001), .rocket(player_control_1_line_1),
    .line_1(line_controler_1_line_1), .line_2(line_controler_1_line_2), .line_3(line_controler_1_line_3),
    .need_value(line_controler_1_need_value), .collision(c1), .restart(St_ch), .clock(graph_clock));
  line_controler line_controler_2 (
    .figure(fig), .Querry_Addr(IOdata[6:4]), .Line_Addr(3'b010), .rocket(player_control_1_line_2),
    .line_1(line_controler_2_line_1), .line_2(line_controler_2_line_2), .line_3(line_controler_2_line_3),
    .need_value(line_controler_2_need_value), .collision(c2), .restart(St_ch), .clock(graph_clock));
  line_controler line_controler_3 (
    .figure(fig), .Querry_Addr(IOdata[6:4]), .Line_Addr(3'b011), .rocket(player_control_1_line_3),
    .line_1(line_controler_3_line_1), .line_2(line_controler_3_line_2), .line_3(line_controler_3_line_3),
    .need_value(line_controler_3_need_value), .collision(c3), .restart(St_ch), .clock(graph_clock));
  line_controler line_controler_4 (
    .figure(fig), .Querry_Addr(IOdata[6:4]), .Line_Addr(3'b100), .rocket(player_control_1_line_4),
    .line_1(line_controler_4_line_1), .line_2(line_controler_4_line_2), .line_3(line_controler_4_line_3),
    .need_value(line_controler_4_need_value), .collision(c4), .restart(St_ch), .clock(graph_clock));
  DotMatrix #(.matrixcols(8), .matrixrows(1)) dotmatrix_2 (
    .col0(hp_1_cell_4_1), .col1(hp_1_cell_4_2), .col2(hp_1_cell_3_1), .col3(hp_1_cell_3_2),
    .col4(hp_1_cell_2_1), .col5(hp_1_cell_2_2), .col6(hp_1_cell_1_1), .col7(hp_1_cell_1_2));
  hp hp_1 (
    .collision(or_5_out), .cell_4_1(hp_1_cell_4_1), .cell_4_2(hp_1_cell_4_2), .cell_3_1(hp_1_cell_3_1),
    .cell_3_2(hp_1_cell_3_2), .cell_2_1(hp_1_cell_2_1), .cell_2_2(hp_1_cell_2_2), .cell_1_1(hp_1_cell_1_1),
    .cell_1_2(hp_1_cell_1_2), .restart(St_ch), .stop(death));
  or or_5 (or_5_out, c4, c3, c2, c1);
  query_filter query_filter_1 (
    .line1(line_controler_1_need_value), .line__2(line_controler_2_need_value),
    .line_3(line_controler_3_need_value), .line_4(line_controler_4_need_value),
    .filtered(query_filter_1_filtered));
  not not_1 (not_1_out, ld);
  assign controlled_buffer_4_out = not_1_out ? D : 8'bz;  // Controlled_Buffer controlled_buffer_4
  assign D = ld ? io_device_1_out : 8'bz;  // Controlled_Buffer controlled_buffer_5
  // CdM_8_mark5 cdm_8_mark5_1: pin names not known; wires that end beside it: cdm_8_mark5_1_p1, cdm_8_mark5_1_p1, cdm_8_mark5_1_p3, cdm_8_mark5_1_p3, proc_clock, cdm_8_mark5_1_p6, cdm_8_mark5_1_p6, cdm_8_mark5_1_p8, cdm_8_mark5_1_p8, cdm_8_mark5_1_p10, cdm_8_mark5_1_p10, cdm_8_mark5_1_p12, cdm_8_mark5_1_p12, cdm_8_mark5_1_p14, cdm_8_mark5_1_p15, ld, A, cdm_8_mark5_1_p18, cdm_8_mark5_1_p19, cdm_8_mark5_1_p20, cdm_8_mark5_1_p20, A[4], A[5], A[6], A[7]
  IO_device io_device_1 (
    .ld(ld), .In(controlled_buffer_4_out), .Adr(A), .Out(io_device_1_out), .sel(IOsel), .clock(ran_clock),
    .IOdata({IOdata, fig}), .query({2'b00, r, query_filter_1_filtered}));
  Decoder #(.disabled(0)) decoder_1 (.out0(code), .out1(data), .sel(cdm_8_mark5_1_p14), .en(cdm_8_mark5_1_p15));
  assign D = not_2_out ? cdm_8_mark5_1_p18 : 8'bz;  // Controlled_Buffer controlled_buffer_6
  not not_2 (not_2_out, ld);
  assign cdm_8_mark5_1_p19 = ld ? D : 8'bz;  // Controlled_Buffer controlled_buffer_7
  and and_1 (IOsel, ~sel, data);  // AND_Gate
  and and_2 (sel, ~A[4], ~A[5], ~A[6], ~A[7], data);  // AND_Gate
  RAM ram_1 (.addr(A), .data(D), .sel(sel), .clk(proc_clock), .ld(ld));  // open: clr
  ROM rom_1 (.addr(A), .data(D), .sel(code));

  // Other names for the same wires on the sheet: IOdata[2:0] = fig; LineAdr[2:0] = IOdata[6:4]

  // Notes on the sheet:
  //   Address_filter
  //   contents of rom_1 (hex, n*v repeats v):
  //   f e1 8f d1 80 b5 d0 f0 44 d2 1 46 e0 28 d2 81 ba 0 e1 18 d2 0 ee 18 a e1 26 d3 10 d2 82 ba 1e d3 83
  //   ae ee 26 ee 28 d2 2 46 e0 49 d2 81 ba d3 10 73 e1 39 d2 0 ee 39 a e1 47 d3 20 d2 82 ba 1e d3 83 ae
  //   ee 47 ee 49 d2 4 46 e0 6a d2 81 ba d3 20 73 e1 5a d2 0 ee 5a a e1 68 d3 30 d2 82 ba 1e d3 83 ae ee
  //   68 ee 6a d2 8 46 e0 8b d2 81 ba d3 30 73 e1 7b d2 0 ee 7b a e1 89 d3 40 d2 82 ba 1e d3 83 ae ee 89
  //   ee 8b d3 0 ee 0 d4
endmodule

module player_control (
  input  left_button,
  input  right_button,
  input  restart,
  output [11:0] line_1,
  output [11:0] line_2,
  output [11:0] line_3,
  output [11:0] line_4,
  output [1:0] active_line_code
);

  wire not_1_out, pull_resistor_1_node, pull_resistor_2_node, pull_resistor_3_node;

  Pull_Resistor #(.pull(1)) pull_resistor_1 (.node(pull_resistor_1_node));
  Pull_Resistor pull_resistor_2 (.node(pull_resistor_2_node));
  assign pull_resistor_2_node = left_button ? 1'b1 : 1'bz;  // Controlled_Buffer controlled_buffer_1
  Demultiplexer #(.select(2), .width(12)) demultiplexer_1 (
    .out0(line_1), .out1(line_2), .out2(line_3), .out3(line_4), .in(12'he7e), .sel(active_line_code),
    .en(pull_resistor_3_node));
  Pull_Resistor #(.pull(1)) pull_resistor_3 (.node(pull_resistor_3_node));
  Counter #(.width(2), .max('h3), .ongoal("stay")) counter_1 (
    .load(not_1_out), .count(pull_resistor_1_node), .Q(active_line_code), .clk(pull_resistor_2_node),
    .clr(restart));  // open: D, carry
  assign pull_resistor_2_node = right_button ? 1'b1 : 1'bz;  // Controlled_Buffer controlled_buffer_2
  not not_1 (not_1_out, right_button);
endmodule

module line_proccesor (
  input  [3:0] l1,
  input  [3:0] l2,
  input  load,
  input  [3:0] l3,
  input  [11:0] rocket,
  input  clock,
  input  restart,
  output [31:0] line_1,
  output [31:0] line_2,
  output need_value,
  output [31:0] line_3,
  output collision
);

  wire and_1_out, comparator_1_eq, comparator_2_eq, comparator_3_eq, comparator_4_eq, comparator_5_eq,
       comparator_6_eq, comparator_7_eq, comparator_8_eq, not_1_out, not_2_out, not_3_out, not_4_out,
       not_5_out, or_1_out, or_5_out;
  wire [3:0] bot_l1, bot_l2, bot_l3;
  wire [31:0] inl1, inl2, inl3, l1out, l2out, l3out, shifter_1_out, shifter_2_out, shifter_3_out;

  Shifter #(.width(32), .shift("lr")) shifter_1 (.in({line_1[31:4], bot_l1}), .\dist (5'b00001), .out(shifter_1_out));
  Shifter #(.width(32), .shift("lr")) shifter_2 (.in({line_2[31:4], bot_l2}), .\dist (5'b00001), .out(shifter_2_out));
  Shifter #(.width(32), .shift("lr")) shifter_3 (.in({line_3[31:4], bot_l3}), .\dist (5'b00001), .out(shifter_3_out));
  Multiplexer #(.width(32), .enable("false")) multiplexer_1 (
    .in0(shifter_1_out), .in1({l1, line_1[27:4], bot_l1}), .out(inl1), .sel(load));
  Multiplexer #(.width(32), .enable("false")) multiplexer_2 (
    .in0(shifter_2_out), .in1({l2, line_2[27:4], bot_l2}), .out(inl2), .sel(load));
  Comparator #(.width(4)) comparator_1 (.a(l2), .b(4'b0000), .eq(comparator_1_eq));  // open: gt, lt
  Multiplexer #(.width(32), .enable("false")) multiplexer_3 (
    .in0(shifter_3_out), .in1({l3, line_3[27:4], bot_l3}), .out(inl3), .sel(load));
  Register #(.width(32), .trigger("falling")) register_1 (
    .D(l1out), .Q({line_1[31:4], bot_l1}), .clk(or_1_out), .clr(restart));  // open: en
  Register #(.width(32), .trigger("falling")) register_2 (
    .D(l2out), .Q({line_2[31:4], bot_l2}), .clk(or_1_out), .clr(restart));  // open: en
  or or_1 (or_1_out, clock, and_1_out);
  and and_1 (and_1_out, not_1_out, load);
  not not_1 (not_1_out, comparator_1_eq);
  Register #(.width(32), .trigger("falling")) register_3 (
    .D(l3out), .Q({line_3[31:4], bot_l3}), .clk(or_1_out), .clr(restart));  // open: en
  Comparator #(.width(4)) comparator_2 (.a(bot_l1), .b(4'b0000), .eq(comparator_2_eq));  // open: gt, lt
  Comparator #(.width(4)) comparator_3 (.a(bot_l2), .b(4'b0000), .eq(comparator_3_eq));  // open: gt, lt
  Comparator #(.width(4)) comparator_4 (.a(bot_l3), .b(4'b0000), .eq(comparator_4_eq));  // open: gt, lt
  Comparator #(.width(12)) comparator_5 (.a(rocket), .b({12{1'b0}}), .eq(comparator_5_eq));  // open: gt, lt
  not not_2 (not_2_out, comparator_2_eq);
  not not_3 (not_3_out, comparator_3_eq);
  not not_4 (not_4_out, comparator_4_eq);
  not not_5 (not_5_out, comparator_5_eq);
  assign line_1[3:0] = rocket[3:0] | bot_l1;  // OR_Gate or_2, 4 bits wide
  assign line_2[3:0] = rocket[7:4] | bot_l2;  // OR_Gate or_3, 4 bits wide
  assign line_3[3:0] = rocket[11:8] | bot_l3;  // OR_Gate or_4, 4 bits wide
  or or_5 (or_5_out, not_2_out, not_3_out, not_4_out);
  and and_2 (collision, or_5_out, not_5_out);
  Multiplexer #(.width(32), .enable("false")) multiplexer_4 (
    .in0(inl1), .in1({inl1[31:8], {8{1'b0}}}), .out(l1out), .sel(collision));
  Multiplexer #(.width(32), .enable("false")) multiplexer_5 (
    .in0(inl2), .in1({inl2[31:8], {8{1'b0}}}), .out(l2out), .sel(collision));
  Multiplexer #(.width(32), .enable("false")) multiplexer_6 (
    .in0(inl3), .in1({inl3[31:8], {8{1'b0}}}), .out(l3out), .sel(collision));
  Comparator #(.width(12)) comparator_6 (.a(line_1[31:20]), .b({12{1'b0}}), .eq(comparator_6_eq));  // open: gt, lt
  Comparator #(.width(12)) comparator_7 (.a(line_2[31:20]), .b({12{1'b0}}), .eq(comparator_7_eq));  // open: gt, lt
  Comparator #(.width(12)) comparator_8 (.a(line_3[31:20]), .b({12{1'b0}}), .eq(comparator_8_eq));  // open: gt, lt
  and and_3 (need_value, comparator_6_eq, comparator_7_eq, comparator_8_eq);

  // Other names for the same wires on the sheet: cl = clock; r1[3:0] = rocket[3:0]; r2[3:0] = rocket[7:4];
  //   r3[3:0] = rocket[11:8]; rt = restart
endmodule

module figure_get (
  input  [2:0] in_1,
  output [11:0] out
);

  DotMatrix #(.matrixcols(3), .matrixrows(4)) dotmatrix_1 (.col0(4'b1000), .col1(4'b1111), .col2(4'b1000));
  DotMatrix #(.matrixcols(3), .matrixrows(4)) dotmatrix_2 (.col0(4'b0000), .col1(4'b1110), .col2(4'b0110));
  DotMatrix #(.matrixcols(3), .matrixrows(4)) dotmatrix_3 (.col0(4'b0000), .col1(4'b1100), .col2(4'b1110));
  DotMatrix #(.matrixcols(3), .matrixrows(4)) dotmatrix_4 (.col0(4'b1000), .col1(4'b1011), .col2(4'b0011));
  DotMatrix #(.matrixcols(3), .matrixrows(4)) dotmatrix_5 (.col0(4'b0010), .col1(4'b0111), .col2(4'b1010));
  DotMatrix #(.matrixcols(3), .matrixrows(4)) dotmatrix_6 (.col0(4'b0001), .col1(4'b1011), .col2(4'b1100));
  DotMatrix #(.matrixcols(3), .matrixrows(4)) dotmatrix_7 (.col0(4'b0001), .col1(4'b0011), .col2(4'b1011));
  DotMatrix #(.matrixcols(3), .matrixrows(4)) dotmatrix_8 (.col0(4'b0100), .col1(4'b1110), .col2(4'b0100));
  Multiplexer #(.select(3), .width(12), .enable("false")) multiplexer_1 (
    .in0(12'h4e4), .in1(12'h13b), .in2(12'h1bc), .in3(12'h27a), .in4(12'h8b3), .in5(12'hce), .in6(12'he6),
    .in7(12'h8f8), .out(out), .sel(in_1));
endmodule

module query_filter (
  input  line1,
  input  line__2,
  input  line_3,
  input  line_4,
  output [3:0] filtered
);

  Multiplexer #(.select(4), .width(4), .disabled(0), .enable("false")) multiplexer_1 (
    .in0(4'b0000), .in1(4'b0000), .in2(4'b0000), .in3(4'b0001), .in4(4'b0000), .in5(4'b0100), .in6(4'b0010),
    .in7(4'b0101), .in8(4'b0000), .in9(4'b0001), .in10(4'b0010), .in11(4'b1001), .in12(4'b0100),
    .in13(4'b1100), .in14(4'b1010), .in15(4'b1101), .out(filtered), .sel({line_4, line_3, line__2, line1}));
endmodule

module hp (
  input  collision,
  input  restart,
  output cell_4_1,
  output cell_4_2,
  output cell_3_1,
  output cell_3_2,
  output cell_2_1,
  output cell_2_2,
  output cell_1_1,
  output cell_1_2,
  output stop
);

  wire and_1_out;
  wire [2:0] counter_1_q;

  Counter #(.width(3), .max('h4), .ongoal("stay")) counter_1 (
    .Q(counter_1_q), .clk(collision), .clr(restart));  // open: load, D, count, carry
  Multiplexer #(.select(3), .width(4), .enable("false")) multiplexer_1 (
    .in0(4'b1111), .in1(4'b1110), .in2(4'b1100), .in3(4'b1000), .in4(4'b0000),
    .out({cell_1_1, cell_2_1, cell_3_1, cell_4_1}), .sel(counter_1_q));  // open: in5, in6, in7
  and and_1 (and_1_out, ~cell_1_1, ~cell_2_1, ~cell_3_1, ~cell_4_1);  // AND_Gate
  T_Flip_Flop t_ff_1 (.clk(and_1_out), .T(1'b1), .Q(stop), .reset(stop));  // open: Qn, preset, en

  assign cell_1_2 = cell_1_1;
  assign cell_2_2 = cell_2_1;
  assign cell_3_2 = cell_3_1;
  assign cell_4_2 = cell_4_1;
endmodule

module state_control (
  input  change_state,
  output state,
  output state_changed
);

  Counter #(.width(1), .max('h1)) counter_1 (.Q(state), .clk(change_state));  // open: load, D, count, carry, clr
  T_Flip_Flop t_ff_1 (.clk(state), .T(1'b1), .Q(state_changed), .reset(state_changed));  // open: Qn, preset, en
endmodule

module line_controler (
  input  [2:0] figure,
  input  [2:0] Querry_Addr,
  input  [2:0] Line_Addr,
  input  restart,
  input  [11:0] rocket,
  input  clock,
  output [31:0] line_1,
  output [31:0] line_2,
  output [31:0] line_3,
  output need_value,
  output collision
);

  wire pull_resistor_1_node;
  wire [2:0] register_1_q;
  wire [11:0] figure_get_1_out;

  Register #(.width(3), .trigger("high")) register_1 (
    .D(figure), .Q(register_1_q), .clk(pull_resistor_1_node), .clr(restart));  // open: en
  Pull_Resistor pull_resistor_1 (.node(pull_resistor_1_node));
  Comparator #(.width(3)) comparator_1 (.a(Querry_Addr), .b(Line_Addr), .eq(pull_resistor_1_node));  // open: gt, lt
  figure_get figure_get_1 (.in_1(register_1_q), .out(figure_get_1_out));
  line_proccesor line_proccesor_1 (
    .l1(figure_get_1_out[3:0]), .load(pull_resistor_1_node), .l2(figure_get_1_out[7:4]),
    .l3(figure_get_1_out[11:8]), .rocket(rocket), .line_1(line_1), .line_2(line_2), .line_3(line_3),
    .need_value(need_value), .clock(clock), .collision(collision), .restart(restart));
endmodule

module light_years_count (
  input  clock,
  input  restart,
  output [3:0] thousand,
  output [3:0] hundred,
  output [3:0] ten,
  output [3:0] unit
);

  wire counter_1_carry, counter_2_carry, counter_3_carry;

  Counter #(.width(4), .max('h9)) counter_1 (
    .Q(unit), .carry(counter_1_carry), .clk(clock), .clr(restart));  // open: load, D, count
  Counter #(.width(4), .max('h9), .trigger("falling")) counter_2 (
    .Q(ten), .carry(counter_2_carry), .clk(counter_1_carry), .clr(restart));  // open: load, D, count
  Counter #(.width(4), .max('h9), .trigger("falling")) counter_3 (
    .Q(hundred), .carry(counter_3_carry), .clk(counter_2_carry), .clr(restart));  // open: load, D, count
  Counter #(.width(4), .max('h9), .trigger("falling")) counter_4 (
    .Q(thousand), .clk(counter_3_carry), .clr(restart));  // open: load, D, count, carry
endmodule

module keyboard_translator (
  input  [6:0] keyboard,
  output left,
  output right,
  output start_stop
);

  Comparator #(.width(7)) comparator_1 (.a(7'b1100001), .b(keyboard), .eq(left));  // open: gt, lt
  Comparator #(.width(7)) comparator_2 (.a(7'b1100100), .b(keyboard), .eq(right));  // open: gt, lt
  Comparator #(.width(7)) comparator_3 (.a(7'b0100000), .b(keyboard), .eq(start_stop));  // open: gt, lt
endmodule

module IO_device (
  input  [7:0] query,
  input  ld,
  input  [7:0] In,
  input  [7:0] Adr,
  input  sel,
  input  clock,
  output [7:0] IOdata,
  output [7:0] Out
);

  wire not_1_out;
  wire [2:0] random_1_out, random_2_out;
  wire [7:0] controlled_buffer_1_out, controlled_buffer_4_out, multiplexer_1_out;

  assign controlled_buffer_1_out = not_1_out ? In : 8'bz;  // Controlled_Buffer controlled_buffer_1
  not not_1 (not_1_out, ld);
  assign Out = ld ? controlled_buffer_4_out : 8'bz;  // Controlled_Buffer controlled_buffer_2
  assign IOdata = sel ? controlled_buffer_1_out : 8'bz;  // Controlled_Buffer controlled_buffer_3
  assign controlled_buffer_4_out = sel ? multiplexer_1_out : 8'bz;  // Controlled_Buffer controlled_buffer_4
  Multiplexer #(.select(2), .width(8), .enable("false")) multiplexer_1 (
    .in0(query), .in1({{5{1'b0}}, random_2_out}), .in2({{5{1'b0}}, random_1_out}), .out(multiplexer_1_out),
    .sel(Adr[1:0]));  // open: in3
  Random #(.width(3)) random_1 (.clk(clock), .out(random_1_out));  // open: next, clr
  Random #(.width(3), .seed(1)) random_2 (.clk(clock), .out(random_2_out));  // open: next, clr

  // Other names for the same wires on the sheet: A[7:0] = Adr; IOsel = sel; ran_clock = clock
endmodule
